// Logisim project ALU_Liberary.circ as structural Verilog: 20 circuits, main circuit 3_BIT_SHR
module _3_BIT_SHR (
  input  [2:0] Input,
  input  [1:0] Shift,
  output [2:0] out_3
);

  Multiplexer #(.select(2), .enable("false")) multiplexer_1 (
    .in0(Input[2]), .in1(1'b0), .in2(1'b0), .in3(1'b0), .out(out_3[2]), .sel(Shift));
  Multiplexer #(.select(2), .enable("false")) multiplexer_2 (
    .in0(Input[1]), .in1(Input[2]), .in2(1'b0), .in3(1'b0), .out(out_3[1]), .sel(Shift));
  Multiplexer #(.select(2), .enable("false")) multiplexer_3 (
    .in0(Input[0]), .in1(Input[1]), .in2(Input[2]), .in3(1'b0), .out(out_3[0]), .sel(Shift));

  // Other names for the same wires on the sheet: A0 = Input[0]; A1 = Input[1]; A2 = Input[2]; O0 = out_3[0];
  //   O1 = out_3[1]; O2 = out_3[2]
endmodule

module ALU (
  input  [2:0] in_1,
  input  [2:0] in_2,
  input  Op,
  output [2:0] out_4,
  output SF,
  output CF,
  output ZF
);

  wire or_1_out;
  wire [2:0] n3_bit_shr_1_out_3, not_2_1_out_2;

  not_2 not_2_1 (.in_1(in_2), .out_2(not_2_1_out_2));
  _3_BIT_SHR u_3_bit_shr_1 (.Input(in_2), .Shift(in_2[1:0]), .out_3(n3_bit_shr_1_out_3));
  Multiplexer #(.width(3), .enable("false")) multiplexer_1 (
    .in0(not_2_1_out_2), .in1(n3_bit_shr_1_out_3), .out(out_4), .sel(Op));
  or or_1 (or_1_out, out_4[2], out_4[1], out_4[0]);
  not not_1 (ZF, or_1_out);

  assign CF = 1'b1;
  assign SF = out_4[2];

  // Other names for the same wires on the sheet: A[2:0] = in_2; SHIFT[1:0] = in_2[1:0]; B[2:0] = in_1
endmodule

module not_2 (
  input  [2:0] in_1,
  output [2:0] out_2
);

  not not_1 (out_2[2], in_1[2]);
  not not_2 (out_2[1], in_1[1]);
  not not_3 (out_2[0], in_1[0]);

  // Other names for the same wires on the sheet: A0 = in_1[0]; A1 = in_1[1]; A2 = in_1[2]
endmodule

module _1_bit_Register (
  input  Din,
  input  Sel,
  input  Clk,
  output Dout
);

  wire multiplexer_1_out;

  Multiplexer #(.enable("false")) multiplexer_1 (.in0(Dout), .in1(Din), .out(multiplexer_1_out), .sel(Sel));
  D_Flip_Flop d_ff_1 (.clk(Clk), .D(multiplexer_1_out), .Q(Dout));  // open: Qn, preset, en, reset
endmodule

module _3_bit_register (
  input  [2:0] Din_2_0,
  input  Sel,
  input  Clk,
  output [2:0] Dout_2_0
);

  _1_bit_Register u_1_bit_register_1 (.Din(Din_2_0[0]), .Sel(Sel), .Clk(Clk), .Dout(Dout_2_0[0]));
  _1_bit_Register u_1_bit_register_2 (.Din(Din_2_0[1]), .Sel(Sel), .Clk(Clk), .Dout(Dout_2_0[1]));
  _1_bit_Register u_1_bit_register_3 (.Din(Din_2_0[2]), .Sel(Sel), .Clk(Clk), .Dout(Dout_2_0[2]));
endmodule

module _6_3_bit_register_set (
  input  Reg_en,
  input  [2:0] Wr,
  input  [2:0] Wrd,
  input  [2:0] Ra,
  input  Clk,
  input  [2:0] Rb,
  output [2:0] out_7,
  output [2:0] out_8
);

  wire Reg0, Reg1, Reg2, Reg3, Reg4, Reg5;
  wire [2:0] R0, R1, R2, R3, R4, R5;

  Decoder #(.select(3)) decoder_1 (
    .out0(Reg0), .out1(Reg1), .out2(Reg2), .out3(Reg3), .out4(Reg4), .out5(Reg5), .sel(Wr), .en(Reg_en));  // open: out6, out7
  _3_bit_register u_3_bit_register_1 (.Din_2_0(Wrd), .Sel(Reg0), .Clk(Clk), .Dout_2_0(R0));
  _3_bit_register u_3_bit_register_2 (.Din_2_0(Wrd), .Sel(Reg1), .Clk(Clk), .Dout_2_0(R1));
  _3_bit_register u_3_bit_register_3 (.Din_2_0(Wrd), .Sel(Reg2), .Clk(Clk), .Dout_2_0(R2));
  _3_bit_register u_3_bit_register_4 (.Din_2_0(Wrd), .Sel(Reg3), .Clk(Clk), .Dout_2_0(R3));
  _3_bit_register u_3_bit_register_5 (.Din_2_0(Wrd), .Sel(Reg4), .Clk(Clk), .Dout_2_0(R4));
  _3_bit_register u_3_bit_register_6 (.Din_2_0(Wrd), .Sel(Reg5), .Clk(Clk), .Dout_2_0(R5));
  Multiplexer #(.select(3), .width(3), .enable("false")) multiplexer_1 (
    .in0(R0), .in1(R1), .in2(R2), .in3(R3), .in4(R4), .in5(R5), .out(out_7), .sel(Ra));  // open: in6, in7
  Multiplexer #(.select(3), .width(3), .enable("false")) multiplexer_2 (
    .in0(R0), .in1(R1), .in2(R2), .in3(R3), .in4(R4), .in5(R5), .out(out_8), .sel(Rb));  // open: in6, in7
endmodule

module _1X1_static_Ram_sel (
  input  Read_Select_1,
  input  Read_Select_2,
  input  Write_Data,
  input  Write_Select,
  input  Clk,
  output Read_Data_1,
  output Read_Data_2
);

  wire d_ff_1_q, multiplexer_1_out;

  Multiplexer #(.enable("false")) multiplexer_1 (
    .in0(d_ff_1_q), .in1(Write_Data), .out(multiplexer_1_out), .sel(Write_Select));
  D_Flip_Flop d_ff_1 (.clk(Clk), .D(multiplexer_1_out), .Q(d_ff_1_q));  // open: Qn, preset, en, reset
  and and_1 (Read_Data_1, Read_Select_1, d_ff_1_q);
  and and_2 (Read_Data_2, Read_Select_2, d_ff_1_q);
endmodule

module _1x6_s_ram (
  input  Read_Select_2,
  input  Read_Select_1,
  input  Write_Select,
  input  [5:0] Write_data,
  input  Clock,
  output [5:0] Read_1,
  output [5:0] Read_2
);

  _1X1_static_Ram_sel u_1x1_static_ram_sel_1 (
    .Write_Data(Write_data[0]), .Write_Select(Write_Select), .Clk(Clock), .Read_Data_1(Read_1[0]),
    .Read_Data_2(Read_2[0]), .Read_Select_1(Read_Select_1), .Read_Select_2(Read_Select_2));
  _1X1_static_Ram_sel u_1x1_static_ram_sel_2 (
    .Write_Data(Write_data[1]), .Write_Select(Write_Select), .Clk(Clock), .Read_Data_1(Read_1[1]),
    .Read_Data_2(Read_2[1]), .Read_Select_1(Read_Select_1), .Read_Select_2(Read_Select_2));
  _1X1_static_Ram_sel u_1x1_static_ram_sel_3 (
    .Write_Data(Write_data[2]), .Write_Select(Write_Select), .Clk(Clock), .Read_Data_1(Read_1[2]),
    .Read_Data_2(Read_2[2]), .Read_Select_1(Read_Select_1), .Read_Select_2(Read_Select_2));
  _1X1_static_Ram_sel u_1x1_static_ram_sel_4 (
    .Write_Data(Write_data[3]), .Write_Select(Write_Select), .Clk(Clock), .Read_Data_1(Read_1[3]),
    .Read_Data_2(Read_2[3]), .Read_Select_1(Read_Select_1), .Read_Select_2(Read_Select_2));
  _1X1_static_Ram_sel u_1x1_static_ram_sel_5 (
    .Write_Data(Write_data[4]), .Write_Select(Write_Select), .Clk(Clock), .Read_Data_1(Read_1[4]),
    .Read_Data_2(Read_2[4]), .Read_Select_1(Read_Select_1), .Read_Select_2(Read_Select_2));
  _1X1_static_Ram_sel u_1x1_static_ram_sel_6 (
    .Write_Data(Write_data[5]), .Write_Select(Write_Select), .Clk(Clock), .Read_Data_1(Read_1[5]),
    .Read_Data_2(Read_2[5]), .Read_Select_1(Read_Select_1), .Read_Select_2(Read_Select_2));

  // Notes on the sheet:
  //   ram_0
  //   ram1
  //   ram2
  //   ram3
  //   ram4
  //   ram5
endmodule

module _1x18_s_Ram (
  input  Read_Select_1,
  input  Read_Select_2,
  input  Write_Select,
  input  Clock,
  input  [17:0] Write_Data,
  output [17:0] Read_2,
  output [17:0] Read_1
);

  _1x6_s_ram u_1x6_s_ram_1 (
    .Read_Select_2(Read_Select_2), .Read_Select_1(Read_Select_1), .Write_Select(Write_Select),
    .Write_data(Write_Data[5:0]), .Clock(Clock), .Read_1(Read_1[5:0]), .Read_2(Read_2[5:0]));
  _1x6_s_ram u_1x6_s_ram_2 (
    .Read_Select_2(Read_Select_2), .Read_Select_1(Read_Select_1), .Write_Select(Write_Select),
    .Write_data(Write_Data[11:6]), .Clock(Clock), .Read_1(Read_1[11:6]), .Read_2(Read_2[11:6]));
  _1x6_s_ram u_1x6_s_ram_3 (
    .Read_Select_2(Read_Select_2), .Read_Select_1(Read_Select_1), .Write_Select(Write_Select),
    .Write_data(Write_Data[17:12]), .Clock(Clock), .Read_1(Read_1[17:12]), .Read_2(Read_2[17:12]));

  // Notes on the sheet:
  //   Ram-0
  //   Ram-1
  //   Ram-2
endmodule

module _8x18_S_Ram (
  input  [17:0] Write_Data__17_0,
  input  Write_Enable,
  input  [2:0] Write_Address_2_0,
  input  [2:0] Read_Address_2_0,
  input  [2:0] Write_Address_2_0_2,
  input  Clock,
  output [17:0] Read_data_1,
  output [17:0] Read_data_2
);

  wire R1_0, R1_1, R1_2, R1_3, R1_4, R1_5, R1_6, R1_7, R2_0, R2_1, R2_2, R2_3, R2_4, R2_5, R2_6, R2_7, W_0,
       W_1, W_2, W_3, W_4, W_5, W_6, W_7;
  wire [17:0] Rd1_0, Rd1_1, Rd1_2, Rd1_3, Rd1_4, Rd1_5, Rd1_6, Rd1_7, Rd2_0, Rd2_1, Rd2_2, Rd2_3, Rd2_4,
       Rd2_5, Rd2_6, Rd2_7;

  Decoder #(.select(3)) decoder_1 (
    .out0(W_0), .out1(W_1), .out2(W_2), .out3(W_3), .out4(W_4), .out5(W_5), .out6(W_6), .out7(W_7),
    .sel(Write_Address_2_0), .en(Write_Enable));
  Decoder #(.select(3), .enable("false")) decoder_2 (
    .out0(R1_0), .out1(R1_1), .out2(R1_2), .out3(R1_3), .out4(R1_4), .out5(R1_5), .out6(R1_6), .out7(R1_7),
    .sel(Read_Address_2_0));
  Decoder #(.select(3), .enable("false")) decoder_3 (
    .out0(R2_0), .out1(R2_1), .out2(R2_2), .out3(R2_3), .out4(R2_4), .out5(R2_5), .out6(R2_6), .out7(R2_7),
    .sel(Write_Address_2_0_2));
  _1x18_s_Ram u_1x18_s_ram_1 (
    .Read_Select_1(R1_0), .Read_Select_2(R2_0), .Write_Select(W_0), .Clock(Clock),
    .Write_Data(Write_Data__17_0), .Read_2(Rd1_0), .Read_1(Rd2_0));
  _1x18_s_Ram u_1x18_s_ram_2 (
    .Read_Select_1(R1_1), .Read_Select_2(R2_1), .Write_Select(W_1), .Clock(Clock),
    .Write_Data(Write_Data__17_0), .Read_2(Rd1_1), .Read_1(Rd2_1));
  _1x18_s_Ram u_1x18_s_ram_3 (
    .Read_Select_1(R1_2), .Read_Select_2(R2_2), .Write_Select(W_2), .Clock(Clock),
    .Write_Data(Write_Data__17_0), .Read_2(Rd1_2), .Read_1(Rd2_2));
  _1x18_s_Ram u_1x18_s_ram_4 (
    .Read_Select_1(R1_3), .Read_Select_2(R2_3), .Write_Select(W_3), .Clock(Clock),
    .Write_Data(Write_Data__17_0), .Read_2(Rd1_3), .Read_1(Rd2_3));
  _1x18_s_Ram u_1x18_s_ram_5 (
    .Read_Select_1(R1_4), .Read_Select_2(R2_4), .Write_Select(W_4), .Clock(Clock),
    .Write_Data(Write_Data__17_0), .Read_2(Rd1_4), .Read_1(Rd2_4));
  _1x18_s_Ram u_1x18_s_ram_6 (
    .Read_Select_1(R1_5), .Read_Select_2(R2_5), .Write_Select(W_5), .Clock(Clock),
    .Write_Data(Write_Data__17_0), .Read_2(Rd1_5), .Read_1(Rd2_5));
  _1x18_s_Ram u_1x18_s_ram_7 (
    .Read_Select_1(R1_6), .Read_Select_2(R2_6), .Write_Select(W_6), .Clock(Clock),
    .Write_Data(Write_Data__17_0), .Read_2(Rd1_6), .Read_1(Rd2_6));
  _1x18_s_Ram u_1x18_s_ram_8 (
    .Read_Select_1(R1_7), .Read_Select_2(R2_7), .Write_Select(W_7), .Clock(Clock),
    .Write_Data(Write_Data__17_0), .Read_2(Rd1_7), .Read_1(Rd2_7));
  assign Read_data_1 = Rd1_0 | Rd1_1 | Rd1_2 | Rd1_3 | Rd1_4 | Rd1_5 | Rd1_6 | Rd1_7;  // OR_Gate or_1, 18 bits wide
  assign Read_data_2 = Rd2_0 | Rd2_1 | Rd2_2 | Rd2_3 | Rd2_4 | Rd2_5 | Rd2_6 | Rd2_7;  // OR_Gate or_2, 18 bits wide
endmodule

module program_counter (
  input  [2:0] I__2_0,
  input  Clock,
  output [2:0] O__2_0
);

  D_Flip_Flop d_ff_1 (.clk(Clock), .D(I__2_0[0]), .Q(O__2_0[0]));  // open: Qn, preset, en, reset
  D_Flip_Flop d_ff_2 (.clk(Clock), .D(I__2_0[1]), .Q(O__2_0[1]));  // open: Qn, preset, en, reset
  D_Flip_Flop d_ff_3 (.clk(Clock), .D(I__2_0[2]), .Q(O__2_0[2]));  // open: Qn, preset, en, reset
endmodule

module Add_count (
  input  [2:0] Input_Address__2_0,
  output [2:0] Output_Address__2_0
);

  wire [2:0] bit_extender_1_out;

  assign bit_extender_1_out = {{2{1'b0}}, 1'b1};  // Bit_Extender bit_extender_1
  Adder #(.width(3)) adder_1 (
    .a(Input_Address__2_0), .b(bit_extender_1_out), .out(Output_Address__2_0), .cin(1'b0));  // open: cout
endmodule

module Rom (
  input  Clock,
  input  PC_Enable,
  output [2:0] Physical_Address,
  output [17:0] Data,
  output Write_Enable,
  output PC_Clock
);

  Counter #(.width(3), .max('h7), .ongoal("stay")) counter_1 (
    .Q(Physical_Address), .clk(Clock));  // open: load, D, count, carry, clr
  not not_1 (Write_Enable, PC_Enable);
  and and_1 (PC_Clock, Clock, PC_Enable);
  ROM #(.addrWidth(3), .dataWidth(18)) rom_1 (.addr(Physical_Address), .data(Data));  // open: sel

  // Notes on the sheet:
  //   contents of rom_1 (hex, n*v repeats v):
  //   a40 9b0 5621 55b0 2e30 39840 5581 38041
endmodule

module CPU (
  input  [2:0] in_1,
  input  [2:0] in_2,
  input  [17:0] in_3,
  input  in_4,
  input  in_5,
  input  in_6
);

  wire alu_1_cf, alu_1_sf, alu_1_zf, CF, CPU_CLK, Imm_Sel, Jmp_Sel, Op, REG_EN, SF, ZF;
  wire [2:0] add_count_1_output_address__2_0, alu_1_out_4, JMP_ST_Data, JNC_ADDRESS, multiplexer_1_out,
       multiplexer_2_out, n6_3_bit_register_set_1_out_8, n8x18_s_ram_1_read_data_1_2, undriven;
  wire [17:0] n8x18_s_ram_1_read_data_1;

  Multiplexer #(.width(3), .disabled(0), .enable("false")) multiplexer_1 (
    .in0(undriven), .in1(JNC_ADDRESS), .out(multiplexer_1_out), .sel(Jmp_Sel));
  Add_count add_count_1 (.Input_Address__2_0(undriven), .Output_Address__2_0(add_count_1_output_address__2_0));
  program_counter program_counter_1 (
    .I__2_0(multiplexer_1_out), .Clock(CPU_CLK), .O__2_0(add_count_1_output_address__2_0));
  and and_1 (CPU_CLK, in_5, in_6);
  _8x18_S_Ram u_8x18_s_ram_1 (
    .Write_Data__17_0(in_3), .Write_Enable(in_4), .Write_Address_2_0(in_2),
    .Read_Address_2_0(add_count_1_output_address__2_0), .Write_Address_2_0_2(in_1), .Clock(in_5),
    .Read_data_1({n8x18_s_ram_1_read_data_1[17:15], JNC_ADDRESS, n8x18_s_ram_1_read_data_1_2, n8x18_s_ram_1_read_data_1[8:0]}));  // open: Read_data_2
  _6_3_bit_register_set u_6_3_bit_register_set_1 (
    .Reg_en(REG_EN), .Wr(JNC_ADDRESS), .Wrd(alu_1_out_4), .Ra(JNC_ADDRESS), .Clk(CPU_CLK),
    .Rb(n8x18_s_ram_1_read_data_1_2), .out_7(JMP_ST_Data), .out_8(n6_3_bit_register_set_1_out_8));
  Flag_Register flag_register_1 (
    .CF(alu_1_cf), .SF(alu_1_sf), .ZF(alu_1_zf), .Clock(CPU_CLK), .CF_2(CF), .SF_2(SF), .ZF_2(ZF));
  ALU alu_1 (
    .in_2(JMP_ST_Data), .Op(Op), .out_4(alu_1_out_4), .SF(alu_1_sf), .CF(alu_1_cf), .ZF(alu_1_zf),
    .in_1(multiplexer_2_out));
  Multiplexer #(.width(3), .disabled(0), .enable("false")) multiplexer_2 (
    .in0(n6_3_bit_register_set_1_out_8), .in1(n8x18_s_ram_1_read_data_1_2), .out(multiplexer_2_out),
    .sel(Imm_Sel));
  my_control my_control_1 (
    .Opcode_2_0(n8x18_s_ram_1_read_data_1[17:15]), .Op_0(Op), .imm_sel(Imm_Sel), .we(REG_EN), .jnc(Jmp_Sel),
    .CF(CF));

  // Other names for the same wires on the sheet: CLK = in_5
endmodule

module Flag_Register (
  input  CF,
  input  SF,
  input  ZF,
  input  Clock,
  output CF_2,
  output SF_2,
  output ZF_2
);

  _1_bit_Register u_1_bit_register_1 (.Din(CF), .Sel(1'b1), .Clk(Clock), .Dout(CF_2));
  _1_bit_Register u_1_bit_register_2 (.Din(SF), .Sel(1'b1), .Clk(Clock), .Dout(SF_2));
  _1_bit_Register u_1_bit_register_3 (.Din(ZF), .Sel(1'b1), .Clk(Clock), .Dout(ZF_2));
endmodule

module my_control (
  input  [2:0] Opcode_2_0,
  input  CF,
  output Op_0,
  output imm_sel,
  output we,
  output jnc
);

  wire Branc_out, not_1_out, not_2_out, not_3_out, not_4_out, not_5_out, we_out;

  not not_1 (not_1_out, Opcode_2_0[0]);
  not not_2 (not_2_out, Opcode_2_0[2]);
  not not_3 (not_3_out, Opcode_2_0[2]);
  not not_4 (not_4_out, Opcode_2_0[1]);
  not not_5 (not_5_out, Opcode_2_0[1]);
  and imm (imm_sel, not_2_out, Opcode_2_0[1]);
  and u_we (we_out, not_3_out, not_4_out);
  and Branc (Branc_out, Opcode_2_0[2], not_5_out);
  or or_1 (we, imm_sel, we_out);
  and u_JNC (jnc, Branc_out, not_1_out, CF);

  assign Op_0 = Opcode_2_0[0];
endmodule

module Temp_rom (
  input  PC_Enable
);

  wire CLK, CPU_CLK, ROM_WE;
  wire [2:0] Phy_Address;
  wire [17:0] ROM_Date;

  Clock Clock (.out(CLK));
  Rom rom_1 (
    .Physical_Address(Phy_Address), .Data(ROM_Date), .Clock(PC_Enable), .Write_Enable(ROM_WE),
    .PC_Clock(CPU_CLK), .PC_Enable(CLK));
endmodule

module Test_alu (
  input  [2:0] in_1,
  input  [2:0] in_2,
  input  in_3,
  output out_4,
  output out_5,
  output out_6,
  output [2:0] out_7
);

  // ALU alu_1: pin names not known; wires that end beside it: in_2, in_3, out_4, out_5, out_6, out_7, in_1
endmodule

module test_register (
  input  [2:0] in_1,
  input  [2:0] in_2,
  input  in_3,
  input  [2:0] in_4,
  input  [2:0] in_5,
  input  in_6,
  output [2:0] out_7,
  output [2:0] out_8
);

  _6_3_bit_register_set u_6_3_bit_register_set_1 (
    .Reg_en(in_3), .Wr(in_5), .Wrd(in_4), .Ra(in_2), .Clk(in_6), .Rb(in_1), .out_7(out_7), .out_8(out_8));
endmodule

module test_ram (
  input  [2:0] in_1,
  input  [2:0] in_2,
  input  [2:0] in_3,
  input  [17:0] in_4,
  input  in_5,
  input  in_6,
  output [17:0] out_7,
  output [17:0] out_8
);

  _8x18_S_Ram u_8x18_s_ram_1 (
    .Write_Data__17_0(in_4), .Write_Enable(in_5), .Write_Address_2_0(in_3), .Read_Address_2_0(in_1),
    .Write_Address_2_0_2(in_2), .Clock(in_6), .Read_data_1(out_7), .Read_data_2(out_8));
endmodule
